# Fritzing sketch schematics (saved by Fritzing 0.9.3b)
breadboards: 1

parts:
  + = Square Pushbutton
  - = Square Pushbutton
  Fan = polarizedheader 4pin 0.156in [package=THT]
  Relay = RELAY [package=relay-g5q]
  DHT22_THERMO = Humidity and Temperature Sensor RHT03
  Pullup = Resistor [tolerance=±5% resistance=4.7k package="2512 [SMD]"]
  PWM = Rectifier Diode [part_number=1N4001 package="300 mil [THT]"]
  Pullup_2 = Resistor [tolerance=±5% resistance=4.7k package=THT]
  MAX7219_DISPLAY = Header 5 [package=1x05-1mm]
  Arduino = Arduino Micro (Rev3)

nets:
  GND: +.leg0, -.leg1, Fan.pin1, Relay.COIL2, DHT22_THERMO.GND_2, MAX7219_DISPLAY.2, Arduino.GND
  N1: +.leg1, Arduino.A0
  N2: -.leg0, Arduino.A1
  +12v: Fan.pin2, Relay.MAIN
  RPM: Fan.pin3, Pullup_2.Pin_0, Arduino.D7
  PWM Signal: Fan.pin4, PWM.cathode
  12V: Relay.NO
  N3: Relay.COIL1, Arduino.D9_PWM/A9
  +5v/5V: DHT22_THERMO.Vcc, Pullup.Pin_0, Pullup_2.Pin_1, MAX7219_DISPLAY.1, Arduino.5V
  N4: DHT22_THERMO.Data-signal, Pullup.Pin_1, Arduino.D4_PWM/A6
  N5: PWM.anode, Arduino.D6_PWM/A7
  DIN: MAX7219_DISPLAY.3, Arduino.MOSI
  CS: MAX7219_DISPLAY.4, Arduino.MISO
  CLK: MAX7219_DISPLAY.5, Arduino.SCK
